// Logisim project 16bitProcessor.circ as structural Verilog: 22 circuits, main circuit 16-bit-registerFile
// Register File
module _16_bit_registerFile (
  input  [3:0] read_register_1,
  input  [3:0] write_register,
  input  [3:0] read_register_2,
  input  [15:0] write_data,
  input  register_write,
  input  clock,
  output [15:0] read_data_1,
  output [15:0] read_data_2
);

  wire and_1_out, and_2_out, and_3_out, and_4_out, and_5_out, and_6_out, and_7_out, and_8_out, and_9_out,
       and_10_out, and_11_out, and_12_out, and_13_out, and_14_out, and_15_out, and_16_out, decoder_1_out0,
       decoder_1_out1, decoder_1_out2, decoder_1_out3, decoder_1_out4, decoder_1_out5, decoder_1_out6,
       decoder_1_out7, decoder_1_out8, decoder_1_out9, decoder_1_out10, decoder_1_out11, decoder_1_out12,
       decoder_1_out13, decoder_1_out14, decoder_1_out15;
  wire [15:0] a0_q, a1_q, ra_q, s0_q, s1_q, s2_q, s3_q, s4_q, s5_q, sp_q, t0_q, t1_q, t2_q, t3_q, v0_q,
       zero_q;

  Decoder #(.select(4)) decoder_1 (
    .out0(decoder_1_out0), .out1(decoder_1_out1), .out2(decoder_1_out2), .out3(decoder_1_out3),
    .out4(decoder_1_out4), .out5(decoder_1_out5), .out6(decoder_1_out6), .out7(decoder_1_out7),
    .out8(decoder_1_out8), .out9(decoder_1_out9), .out10(decoder_1_out10), .out11(decoder_1_out11),
    .out12(decoder_1_out12), .out13(decoder_1_out13), .out14(decoder_1_out14), .out15(decoder_1_out15),
    .sel(write_register));  // open: en
  and and_1 (and_1_out, decoder_1_out0, register_write);
  and and_2 (and_2_out, decoder_1_out1, register_write);
  and and_3 (and_3_out, decoder_1_out2, register_write);
  and and_4 (and_4_out, decoder_1_out3, register_write);
  and and_5 (and_5_out, decoder_1_out4, register_write);
  and and_6 (and_6_out, decoder_1_out5, register_write);
  and and_7 (and_7_out, decoder_1_out6, register_write);
  and and_8 (and_8_out, decoder_1_out7, register_write);
  and and_9 (and_9_out, decoder_1_out8, register_write);
  and and_10 (and_10_out, decoder_1_out9, register_write);
  and and_11 (and_11_out, decoder_1_out10, register_write);
  and and_12 (and_12_out, decoder_1_out11, register_write);
  and and_13 (and_13_out, decoder_1_out12, register_write);
  and and_14 (and_14_out, decoder_1_out13, register_write);
  and and_15 (and_15_out, decoder_1_out14, register_write);
  and and_16 (and_16_out, decoder_1_out15, register_write);
  Register #(.width(16)) zero (.D(write_data), .en(and_1_out), .Q(zero_q), .clk(clock));  // open: clr
  Register #(.width(16)) t0 (.D(write_data), .en(and_2_out), .Q(t0_q), .clk(clock));  // open: clr
  Register #(.width(16)) t1 (.D(write_data), .en(and_3_out), .Q(t1_q), .clk(clock));  // open: clr
  Register #(.width(16)) t2 (.D(write_data), .en(and_4_out), .Q(t2_q), .clk(clock));  // open: clr
  Register #(.width(16)) t3 (.D(write_data), .en(and_5_out), .Q(t3_q), .clk(clock));  // open: clr
  Register #(.width(16)) s0 (.D(write_data), .en(and_6_out), .Q(s0_q), .clk(clock));  // open: clr
  Register #(.width(16)) s1 (.D(write_data), .en(and_7_out), .Q(s1_q), .clk(clock));  // open: clr
  Register #(.width(16)) s2 (.D(write_data), .en(and_8_out), .Q(s2_q), .clk(clock));  // open: clr
  Register #(.width(16)) s3 (.D(write_data), .en(and_9_out), .Q(s3_q), .clk(clock));  // open: clr
  Register #(.width(16)) s4 (.D(write_data), .en(and_10_out), .Q(s4_q), .clk(clock));  // open: clr
  Register #(.width(16)) s5 (.D(write_data), .en(and_11_out), .Q(s5_q), .clk(clock));  // open: clr
  Register #(.width(16)) sp (.D(write_data), .en(and_12_out), .Q(sp_q), .clk(clock));  // open: clr
  Register #(.width(16)) v0 (.D(write_data), .en(and_13_out), .Q(v0_q), .clk(clock));  // open: clr
  Register #(.width(16)) ra (.D(write_data), .en(and_14_out), .Q(ra_q), .clk(clock));  // open: clr
  Register #(.width(16)) a0 (.D(write_data), .en(and_15_out), .Q(a0_q), .clk(clock));  // open: clr
  Register #(.width(16)) a1 (.D(write_data), .en(and_16_out), .Q(a1_q), .clk(clock));  // open: clr
  Multiplexer #(.select(4), .width(16)) multiplexer_1 (
    .in0(zero_q), .in1(t0_q), .in2(t1_q), .in3(t2_q), .in4(t3_q), .in5(s0_q), .in6(s1_q), .in7(s2_q),
    .in8(s3_q), .in9(s4_q), .in10(s5_q), .in11(sp_q), .in12(v0_q), .in13(ra_q), .in14(a0_q), .in15(a1_q),
    .out(read_data_1), .sel(read_register_1));  // open: en
  Multiplexer #(.select(4), .width(16)) multiplexer_2 (
    .in0(zero_q), .in1(t0_q), .in2(t1_q), .in3(t2_q), .in4(t3_q), .in5(s0_q), .in6(s1_q), .in7(s2_q),
    .in8(s3_q), .in9(s4_q), .in10(s5_q), .in11(sp_q), .in12(v0_q), .in13(ra_q), .in14(a0_q), .in15(a1_q),
    .out(read_data_2), .sel(read_register_2));  // open: en
endmodule

// ALU
module _1_bit_ALU (
  input  B,
  input  A,
  input  Carryin,
  input  [2:0] operation,
  input  Binvert,
  output result,
  output carryOut
);

  wire adder_1_out, and_1_out, multiplexer_1_out, nor_1_out, not_1_out, or_1_out, xor_1_out;

  not not_1 (not_1_out, B);
  Multiplexer multiplexer_1 (.in0(not_1_out), .in1(B), .out(multiplexer_1_out), .sel(Binvert));  // open: en
  and and_1 (and_1_out, A, multiplexer_1_out);
  or or_1 (or_1_out, A, multiplexer_1_out);
  nor nor_1 (nor_1_out, A, multiplexer_1_out);
  xor xor_1 (xor_1_out, A, multiplexer_1_out);
  Adder #(.width(1)) adder_1 (.a(A), .b(multiplexer_1_out), .out(adder_1_out), .cin(Carryin), .cout(carryOut));
  Multiplexer #(.select(3)) multiplexer_2 (
    .in0(and_1_out), .in1(or_1_out), .in2(nor_1_out), .in3(xor_1_out), .in4(adder_1_out), .out(result),
    .sel(operation));  // open: in5, in6, in7, en
endmodule

// 16 bit ALU
module _16bit_ALU (
  input  carryin,
  input  [15:0] A,
  input  [15:0] B,
  input  Binvert,
  input  [2:0] operation,
  output [15:0] result,
  output zero,
  output overFlow,
  output carryOut
);

  wire n1_bit_alu_1_carryout, n1_bit_alu_2_carryout, n1_bit_alu_3_carryout, n1_bit_alu_4_carryout,
       n1_bit_alu_5_carryout, n1_bit_alu_6_carryout, n1_bit_alu_7_carryout, n1_bit_alu_8_carryout,
       n1_bit_alu_9_carryout, n1_bit_alu_10_carryout, n1_bit_alu_11_carryout, n1_bit_alu_12_carryout,
       n1_bit_alu_13_carryout, n1_bit_alu_14_carryout, n1_bit_alu_15_carryout;

  _1_bit_ALU u_1_bit_alu_1 (
    .result(result[0]), .B(B[0]), .A(A[0]), .Carryin(carryin), .Binvert(Binvert),
    .carryOut(n1_bit_alu_1_carryout), .operation(operation));
  _1_bit_ALU u_1_bit_alu_2 (
    .result(result[1]), .B(B[1]), .A(A[1]), .Carryin(n1_bit_alu_1_carryout), .Binvert(Binvert),
    .carryOut(n1_bit_alu_2_carryout), .operation(operation));
  _1_bit_ALU u_1_bit_alu_3 (
    .result(result[2]), .B(B[2]), .A(A[2]), .Carryin(n1_bit_alu_2_carryout), .Binvert(Binvert),
    .carryOut(n1_bit_alu_3_carryout), .operation(operation));
  _1_bit_ALU u_1_bit_alu_4 (
    .result(result[3]), .B(B[3]), .A(A[3]), .Carryin(n1_bit_alu_3_carryout), .Binvert(Binvert),
    .carryOut(n1_bit_alu_4_carryout), .operation(operation));
  _1_bit_ALU u_1_bit_alu_5 (
    .result(result[4]), .B(B[4]), .A(A[4]), .Carryin(n1_bit_alu_4_carryout), .Binvert(Binvert),
    .carryOut(n1_bit_alu_5_carryout), .operation(operation));
  _1_bit_ALU u_1_bit_alu_6 (
    .result(result[5]), .B(B[5]), .A(A[5]), .Carryin(n1_bit_alu_5_carryout), .Binvert(Binvert),
    .carryOut(n1_bit_alu_6_carryout), .operation(operation));
  _1_bit_ALU u_1_bit_alu_7 (
    .result(result[6]), .B(B[6]), .A(A[6]), .Carryin(n1_bit_alu_6_carryout), .Binvert(Binvert),
    .carryOut(n1_bit_alu_7_carryout), .operation(operation));
  _1_bit_ALU u_1_bit_alu_8 (
    .result(result[7]), .B(B[7]), .A(A[7]), .Carryin(n1_bit_alu_7_carryout), .Binvert(Binvert),
    .carryOut(n1_bit_alu_8_carryout), .operation(operation));
  _1_bit_ALU u_1_bit_alu_9 (
    .result(result[8]), .B(B[8]), .A(A[8]), .Carryin(n1_bit_alu_8_carryout), .Binvert(Binvert),
    .carryOut(n1_bit_alu_9_carryout), .operation(operation));
  _1_bit_ALU u_1_bit_alu_10 (
    .result(result[9]), .B(B[9]), .A(A[9]), .Carryin(n1_bit_alu_9_carryout), .Binvert(Binvert),
    .carryOut(n1_bit_alu_10_carryout), .operation(operation));
  _1_bit_ALU u_1_bit_alu_11 (
    .result(result[10]), .B(B[10]), .A(A[10]), .Carryin(n1_bit_alu_10_carryout), .Binvert(Binvert),
    .carryOut(n1_bit_alu_11_carryout), .operation(operation));
  _1_bit_ALU u_1_bit_alu_12 (
    .result(result[11]), .B(B[11]), .A(A[11]), .Carryin(n1_bit_alu_11_carryout), .Binvert(Binvert),
    .carryOut(n1_bit_alu_12_carryout), .operation(operation));
  _1_bit_ALU u_1_bit_alu_13 (
    .result(result[12]), .B(B[12]), .A(A[12]), .Carryin(n1_bit_alu_12_carryout), .Binvert(Binvert),
    .carryOut(n1_bit_alu_13_carryout), .operation(operation));
  _1_bit_ALU u_1_bit_alu_14 (
    .result(result[13]), .B(B[13]), .A(A[13]), .Carryin(n1_bit_alu_13_carryout), .Binvert(Binvert),
    .carryOut(n1_bit_alu_14_carryout), .operation(operation));
  _1_bit_ALU u_1_bit_alu_15 (
    .result(result[14]), .B(B[14]), .A(A[14]), .Carryin(n1_bit_alu_14_carryout), .Binvert(Binvert),
    .carryOut(n1_bit_alu_15_carryout), .operation(operation));
  _1_bit_ALU u_1_bit_alu_16 (
    .result(result[15]), .B(B[15]), .A(A[15]), .Carryin(n1_bit_alu_15_carryout), .Binvert(Binvert),
    .carryOut(carryOut), .operation(operation));
  xor xor_1 (overFlow, n1_bit_alu_15_carryout, carryOut);
  nor nor_1 (zero, result[0], result[1], result[2], result[3], result[4], result[5], result[6], result[7], result[8], result[9], result[10], result[11], result[12], result[13], result[14], result[15]);

  // Other names for the same wires on the sheet: R0 = result[0]; R1 = result[1]; R2 = result[2]; R3 = result[3];
  //   R4 = result[4]; R5 = result[5]; R6 = result[6]; R7 = result[7]; R8 = result[8]; R9 = result[9];
  //   R10 = result[10]; R11 = result[11]; R12 = result[12]; R13 = result[13]; R14 = result[14]; R15 = result[15]
endmodule

module sll (
  input  [15:0] data,
  input  [3:0] shift_amount,
  output [15:0] out_data
);

  Multiplexer #(.select(4)) multiplexer_1 (
    .in0(data[0]), .in1(1'b0), .in2(1'b0), .in3(1'b0), .in4(1'b0), .in5(1'b0), .in6(1'b0), .in7(1'b0),
    .in8(1'b0), .in9(1'b0), .in10(1'b0), .in11(1'b0), .in12(1'b0), .in13(1'b0), .in14(1'b0), .in15(1'b0),
    .out(out_data[0]), .sel(shift_amount));  // open: en
  Multiplexer #(.select(4)) multiplexer_2 (
    .in0(data[1]), .in1(data[0]), .in2(1'b0), .in3(1'b0), .in4(1'b0), .in5(1'b0), .in6(1'b0), .in7(1'b0),
    .in8(1'b0), .in9(1'b0), .in10(1'b0), .in11(1'b0), .in12(1'b0), .in13(1'b0), .in14(1'b0), .in15(1'b0),
    .out(out_data[1]), .sel(shift_amount));  // open: en
  Multiplexer #(.select(4)) multiplexer_3 (
    .in0(data[2]), .in1(data[1]), .in2(data[0]), .in3(1'b0), .in4(1'b0), .in5(1'b0), .in6(1'b0), .in7(1'b0),
    .in8(1'b0), .in9(1'b0), .in10(1'b0), .in11(1'b0), .in12(1'b0), .in13(1'b0), .in14(1'b0), .in15(1'b0),
    .out(out_data[2]), .sel(shift_amount));  // open: en
  Multiplexer #(.select(4)) multiplexer_4 (
    .in0(data[3]), .in1(data[2]), .in2(data[1]), .in3(data[0]), .in4(1'b0), .in5(1'b0), .in6(1'b0),
    .in7(1'b0), .in8(1'b0), .in9(1'b0), .in10(1'b0), .in11(1'b0), .in12(1'b0), .in13(1'b0), .in14(1'b0),
    .in15(1'b0), .out(out_data[3]), .sel(shift_amount));  // open: en
  Multiplexer #(.select(4)) multiplexer_5 (
    .in0(data[4]), .in1(data[3]), .in2(data[2]), .in3(data[1]), .in4(data[0]), .in5(1'b0), .in6(1'b0),
    .in7(1'b0), .in8(1'b0), .in9(1'b0), .in10(1'b0), .in11(1'b0), .in12(1'b0), .in13(1'b0), .in14(1'b0),
    .in15(1'b0), .out(out_data[4]), .sel(shift_amount));  // open: en
  Multiplexer #(.select(4)) multiplexer_6 (
    .in0(data[5]), .in1(data[4]), .in2(data[3]), .in3(data[2]), .in4(data[1]), .in5(data[0]), .in6(1'b0),
    .in7(1'b0), .in8(1'b0), .in9(1'b0), .in10(1'b0), .in11(1'b0), .in12(1'b0), .in13(1'b0), .in14(1'b0),
    .in15(1'b0), .out(out_data[5]), .sel(shift_amount));  // open: en
  Multiplexer #(.select(4)) multiplexer_7 (
    .in0(data[6]), .in1(data[5]), .in2(data[4]), .in3(data[3]), .in4(data[2]), .in5(data[1]), .in6(data[0]),
    .in7(1'b0), .in8(1'b0), .in9(1'b0), .in10(1'b0), .in11(1'b0), .in12(1'b0), .in13(1'b0), .in14(1'b0),
    .in15(1'b0), .out(out_data[6]), .sel(shift_amount));  // open: en
  Multiplexer #(.select(4)) multiplexer_8 (
    .in0(data[7]), .in1(data[6]), .in2(data[5]), .in3(data[4]), .in4(data[3]), .in5(data[2]), .in6(data[1]),
    .in7(data[0]), .in8(1'b0), .in9(1'b0), .in10(1'b0), .in11(1'b0), .in12(1'b0), .in13(1'b0), .in14(1'b0),
    .in15(1'b0), .out(out_data[7]), .sel(shift_amount));  // open: en
  Multiplexer #(.select(4)) multiplexer_9 (
    .in0(data[8]), .in1(data[7]), .in2(data[6]), .in3(data[5]), .in4(data[4]), .in5(data[3]), .in6(data[2]),
    .in7(data[1]), .in8(data[0]), .in9(1'b0), .in10(1'b0), .in11(1'b0), .in12(1'b0), .in13(1'b0),
    .in14(1'b0), .in15(1'b0), .out(out_data[8]), .sel(shift_amount));  // open: en
  Multiplexer #(.select(4)) multiplexer_10 (
    .in0(data[9]), .in1(data[8]), .in2(data[7]), .in3(data[6]), .in4(data[5]), .in5(data[4]), .in6(data[3]),
    .in7(data[2]), .in8(data[1]), .in9(data[0]), .in10(1'b0), .in11(1'b0), .in12(1'b0), .in13(1'b0),
    .in14(1'b0), .in15(1'b0), .out(out_data[9]), .sel(shift_amount));  // open: en
  Multiplexer #(.select(4)) multiplexer_11 (
    .in0(data[10]), .in1(data[9]), .in2(data[8]), .in3(data[7]), .in4(data[6]), .in5(data[5]), .in6(data[4]),
    .in7(data[3]), .in8(data[2]), .in9(data[1]), .in10(data[0]), .in11(1'b0), .in12(1'b0), .in13(1'b0),
    .in14(1'b0), .in15(1'b0), .out(out_data[10]), .sel(shift_amount));  // open: en
  Multiplexer #(.select(4)) multiplexer_12 (
    .in0(data[11]), .in1(data[10]), .in2(data[9]), .in3(data[8]), .in4(data[7]), .in5(data[6]),
    .in6(data[5]), .in7(data[4]), .in8(data[3]), .in9(data[2]), .in10(data[1]), .in11(data[0]), .in12(1'b0),
    .in13(1'b0), .in14(1'b0), .in15(1'b0), .out(out_data[11]), .sel(shift_amount));  // open: en
  Multiplexer #(.select(4)) multiplexer_13 (
    .in0(data[12]), .in1(data[11]), .in2(data[10]), .in3(data[9]), .in4(data[8]), .in5(data[7]),
    .in6(data[6]), .in7(data[5]), .in8(data[4]), .in9(data[3]), .in10(data[2]), .in11(data[1]),
    .in12(data[0]), .in13(1'b0), .in14(1'b0), .in15(1'b0), .out(out_data[12]), .sel(shift_amount));  // open: en
  Multiplexer #(.select(4)) multiplexer_14 (
    .in0(data[13]), .in1(data[12]), .in2(data[11]), .in3(data[10]), .in4(data[9]), .in5(data[8]),
    .in6(data[7]), .in7(data[6]), .in8(data[5]), .in9(data[4]), .in10(data[3]), .in11(data[2]),
    .in12(data[1]), .in13(data[0]), .in14(1'b0), .in15(1'b0), .out(out_data[13]), .sel(shift_amount));  // open: en
  Multiplexer #(.select(4)) multiplexer_15 (
    .in0(data[14]), .in1(data[13]), .in2(data[12]), .in3(data[11]), .in4(data[10]), .in5(data[9]),
    .in6(data[8]), .in7(data[7]), .in8(data[6]), .in9(data[5]), .in10(data[4]), .in11(data[3]),
    .in12(data[2]), .in13(data[1]), .in14(data[0]), .in15(1'b0), .out(out_data[14]), .sel(shift_amount));  // open: en
  Multiplexer #(.select(4)) multiplexer_16 (
    .in0(data[15]), .in1(data[14]), .in2(data[13]), .in3(data[12]), .in4(data[11]), .in5(data[10]),
    .in6(data[9]), .in7(data[8]), .in8(data[7]), .in9(data[6]), .in10(data[5]), .in11(data[4]),
    .in12(data[3]), .in13(data[2]), .in14(data[1]), .in15(data[0]), .out(out_data[15]), .sel(shift_amount));  // open: en
endmodule

module srl (
  input  [15:0] in_1,
  input  [3:0] in_2,
  output [15:0] out_3
);

  Multiplexer #(.select(4)) multiplexer_1 (
    .in0(in_1[0]), .in1(in_1[1]), .in2(in_1[2]), .in3(in_1[3]), .in4(in_1[4]), .in5(in_1[5]), .in6(in_1[6]),
    .in7(in_1[7]), .in8(in_1[8]), .in9(in_1[9]), .in10(in_1[10]), .in11(in_1[11]), .in12(in_1[12]),
    .in13(in_1[13]), .in14(in_1[14]), .in15(in_1[15]), .out(out_3[0]), .sel(in_2));  // open: en
  Multiplexer #(.select(4)) multiplexer_2 (
    .in0(in_1[1]), .in1(in_1[2]), .in2(in_1[3]), .in3(in_1[4]), .in4(in_1[5]), .in5(in_1[6]), .in6(in_1[7]),
    .in7(in_1[8]), .in8(in_1[9]), .in9(in_1[10]), .in10(in_1[11]), .in11(in_1[12]), .in12(in_1[13]),
    .in13(in_1[14]), .in14(in_1[15]), .in15(1'b0), .out(out_3[1]), .sel(in_2));  // open: en
  Multiplexer #(.select(4)) multiplexer_3 (
    .in0(in_1[2]), .in1(in_1[3]), .in2(in_1[4]), .in3(in_1[5]), .in4(in_1[6]), .in5(in_1[7]), .in6(in_1[8]),
    .in7(in_1[9]), .in8(in_1[10]), .in9(in_1[11]), .in10(in_1[12]), .in11(in_1[13]), .in12(in_1[14]),
    .in13(in_1[15]), .in14(1'b0), .in15(1'b0), .out(out_3[2]), .sel(in_2));  // open: en
  Multiplexer #(.select(4)) multiplexer_4 (
    .in0(in_1[3]), .in1(in_1[4]), .in2(in_1[5]), .in3(in_1[6]), .in4(in_1[7]), .in5(in_1[8]), .in6(in_1[9]),
    .in7(in_1[10]), .in8(in_1[11]), .in9(in_1[12]), .in10(in_1[13]), .in11(in_1[14]), .in12(in_1[15]),
    .in13(1'b0), .in14(1'b0), .in15(1'b0), .out(out_3[3]), .sel(in_2));  // open: en
  Multiplexer #(.select(4)) multiplexer_5 (
    .in0(in_1[4]), .in1(in_1[5]), .in2(in_1[6]), .in3(in_1[7]), .in4(in_1[8]), .in5(in_1[9]), .in6(in_1[10]),
    .in7(in_1[11]), .in8(in_1[12]), .in9(in_1[13]), .in10(in_1[14]), .in11(in_1[15]), .in12(1'b0),
    .in13(1'b0), .in14(1'b0), .in15(1'b0), .out(out_3[4]), .sel(in_2));  // open: en
  Multiplexer #(.select(4)) multiplexer_6 (
    .in0(in_1[5]), .in1(in_1[6]), .in2(in_1[7]), .in3(in_1[8]), .in4(in_1[9]), .in5(in_1[10]),
    .in6(in_1[11]), .in7(in_1[12]), .in8(in_1[13]), .in9(in_1[14]), .in10(in_1[15]), .in11(1'b0),
    .in12(1'b0), .in13(1'b0), .in14(1'b0), .in15(1'b0), .out(out_3[5]), .sel(in_2));  // open: en
  Multiplexer #(.select(4)) multiplexer_7 (
    .in0(in_1[6]), .in1(in_1[7]), .in2(in_1[8]), .in3(in_1[9]), .in4(in_1[10]), .in5(in_1[11]),
    .in6(in_1[12]), .in7(in_1[13]), .in8(in_1[14]), .in9(in_1[15]), .in10(1'b0), .in11(1'b0), .in12(1'b0),
    .in13(1'b0), .in14(1'b0), .in15(1'b0), .out(out_3[6]), .sel(in_2));  // open: en
  Multiplexer #(.select(4)) multiplexer_8 (
    .in0(in_1[7]), .in1(in_1[8]), .in2(in_1[9]), .in3(in_1[10]), .in4(in_1[11]), .in5(in_1[12]),
    .in6(in_1[13]), .in7(in_1[14]), .in8(in_1[15]), .in9(1'b0), .in10(1'b0), .in11(1'b0), .in12(1'b0),
    .in13(1'b0), .in14(1'b0), .in15(1'b0), .out(out_3[7]), .sel(in_2));  // open: en
  Multiplexer #(.select(4)) multiplexer_9 (
    .in0(in_1[8]), .in1(in_1[9]), .in2(in_1[10]), .in3(in_1[11]), .in4(in_1[12]), .in5(in_1[13]),
    .in6(in_1[14]), .in7(in_1[15]), .in8(1'b0), .in9(1'b0), .in10(1'b0), .in11(1'b0), .in12(1'b0),
    .in13(1'b0), .in14(1'b0), .in15(1'b0), .out(out_3[8]), .sel(in_2));  // open: en
  Multiplexer #(.select(4)) multiplexer_10 (
    .in0(in_1[9]), .in1(in_1[10]), .in2(in_1[11]), .in3(in_1[12]), .in4(in_1[13]), .in5(in_1[14]),
    .in6(in_1[15]), .in7(1'b0), .in8(1'b0), .in9(1'b0), .in10(1'b0), .in11(1'b0), .in12(1'b0), .in13(1'b0),
    .in14(1'b0), .in15(1'b0), .out(out_3[9]), .sel(in_2));  // open: en
  Multiplexer #(.select(4)) multiplexer_11 (
    .in0(in_1[10]), .in1(in_1[11]), .in2(in_1[12]), .in3(in_1[13]), .in4(in_1[14]), .in5(in_1[15]),
    .in6(1'b0), .in7(1'b0), .in8(1'b0), .in9(1'b0), .in10(1'b0), .in11(1'b0), .in12(1'b0), .in13(1'b0),
    .in14(1'b0), .in15(1'b0), .out(out_3[10]), .sel(in_2));  // open: en
  Multiplexer #(.select(4)) multiplexer_12 (
    .in0(in_1[11]), .in1(in_1[12]), .in2(in_1[13]), .in3(in_1[14]), .in4(in_1[15]), .in5(1'b0), .in6(1'b0),
    .in7(1'b0), .in8(1'b0), .in9(1'b0), .in10(1'b0), .in11(1'b0), .in12(1'b0), .in13(1'b0), .in14(1'b0),
    .in15(1'b0), .out(out_3[11]), .sel(in_2));  // open: en
  Multiplexer #(.select(4)) multiplexer_13 (
    .in0(in_1[12]), .in1(in_1[13]), .in2(in_1[14]), .in3(in_1[15]), .in4(1'b0), .in5(1'b0), .in6(1'b0),
    .in7(1'b0), .in8(1'b0), .in9(1'b0), .in10(1'b0), .in11(1'b0), .in12(1'b0), .in13(1'b0), .in14(1'b0),
    .in15(1'b0), .out(out_3[12]), .sel(in_2));  // open: en
  Multiplexer #(.select(4)) multiplexer_14 (
    .in0(in_1[13]), .in1(in_1[14]), .in2(in_1[15]), .in3(1'b0), .in4(1'b0), .in5(1'b0), .in6(1'b0),
    .in7(1'b0), .in8(1'b0), .in9(1'b0), .in10(1'b0), .in11(1'b0), .in12(1'b0), .in13(1'b0), .in14(1'b0),
    .in15(1'b0), .out(out_3[13]), .sel(in_2));  // open: en
  Multiplexer #(.select(4)) multiplexer_15 (
    .in0(in_1[14]), .in1(in_1[15]), .in2(1'b0), .in3(1'b0), .in4(1'b0), .in5(1'b0), .in6(1'b0), .in7(1'b0),
    .in8(1'b0), .in9(1'b0), .in10(1'b0), .in11(1'b0), .in12(1'b0), .in13(1'b0), .in14(1'b0), .in15(1'b0),
    .out(out_3[14]), .sel(in_2));  // open: en
  Multiplexer #(.select(4)) multiplexer_16 (
    .in0(in_1[15]), .in1(1'b0), .in2(1'b0), .in3(1'b0), .in4(1'b0), .in5(1'b0), .in6(1'b0), .in7(1'b0),
    .in8(1'b0), .in9(1'b0), .in10(1'b0), .in11(1'b0), .in12(1'b0), .in13(1'b0), .in14(1'b0), .in15(1'b0),
    .out(out_3[15]), .sel(in_2));  // open: en
endmodule

// Shift unit
module sll_srl (
  input  [15:0] in_1,
  input  [3:0] in_2,
  input  in_3,
  output [15:0] out_4
);

  wire [15:0] sll_1_out_data, srl_1_out_3;

  sll sll_1 (.data(in_1), .shift_amount(in_2), .out_data(sll_1_out_data));
  srl srl_1 (.in_2(in_2), .in_1(in_1), .out_3(srl_1_out_3));
  Multiplexer #(.width(16)) multiplexer_1 (
    .in0(sll_1_out_data), .in1(srl_1_out_3), .out(out_4), .sel(in_3));  // open: en

  // Notes on the sheet:
  //   sll
  //   srl
endmodule

module ALU_demo (
  input  [15:0] A,
  input  [15:0] B,
  input  Binvert,
  input  [2:0] operation,
  input  carryin,
  output overFlow,
  output zero,
  output [15:0] result,
  output carryOut
);

  wire n16bit_alu_1_carryout;

  _16bit_ALU u_16bit_alu_1 (
    .A(A), .B(B), .Binvert(Binvert), .operation(operation), .zero(zero), .overFlow(overFlow),
    .carryOut(n16bit_alu_1_carryout), .carryin(carryin), .result(result));
endmodule

module controlUnit_shift (
  input  [3:0] opCode,
  output shift
);

  wire not_1_out;

  not not_1 (not_1_out, opCode[1]);
  and and_1 (shift, not_1_out, opCode[2], opCode[3]);
endmodule

module controlUnit_LorR (
  input  [3:0] opCode,
  output LorR
);

  wire not_1_out;

  not not_1 (not_1_out, opCode[1]);
  and and_1 (LorR, opCode[0], not_1_out, opCode[2], opCode[3]);
endmodule

module controlUnit_carryin (
  input  [3:0] opCode,
  output carryin
);

  wire and_1_out, and_2_out, not_1_out, not_2_out, not_3_out;

  not not_1 (not_1_out, opCode[1]);
  not not_2 (not_2_out, opCode[2]);
  not not_3 (not_3_out, opCode[3]);
  and and_1 (and_1_out, opCode[0], not_1_out, not_2_out, not_3_out);
  and and_2 (and_2_out, not_3_out, opCode[2], opCode[1], opCode[0]);
  or or_1 (carryin, and_1_out, and_2_out);
endmodule

module controlUnit_Bbar (
  input  [3:0] opCode,
  output Binvert
);

  wire and_1_out, and_2_out, and_3_out, and_4_out, not_1_out, not_2_out, not_3_out, not_4_out;

  not not_1 (not_1_out, opCode[3]);
  not not_2 (not_2_out, opCode[0]);
  not not_3 (not_3_out, opCode[1]);
  not not_4 (not_4_out, opCode[2]);
  and and_1 (and_1_out, not_4_out, opCode[1]);
  and and_2 (and_2_out, not_2_out, opCode[3], opCode[1]);
  and and_3 (and_3_out, opCode[0], not_4_out, opCode[3]);
  and and_4 (and_4_out, not_2_out, not_3_out, not_1_out);
  or or_1 (Binvert, and_1_out, and_2_out, and_3_out, and_4_out);
endmodule

module controlUnit_store (
  input  [3:0] opCode,
  output store
);

  wire not_1_out, not_2_out;

  not not_1 (not_1_out, opCode[0]);
  not not_2 (not_2_out, opCode[3]);
  and and_1 (store, not_1_out, opCode[1], opCode[2], not_2_out);
endmodule

module controlUnit_load (
  input  [3:0] opCode,
  output load
);

  wire not_1_out, not_2_out;

  not not_1 (not_1_out, opCode[1]);
  not not_2 (not_2_out, opCode[3]);
  and and_1 (load, opCode[0], not_1_out, opCode[2], not_2_out);
endmodule

module controlUnit_jump (
  input  [3:0] opCode,
  output jump
);

  and and_1 (jump, opCode[0], opCode[1], opCode[2], opCode[3]);
endmodule

module controlUnit_branch (
  input  [3:0] opCode,
  output branch
);

  wire not_1_out;

  not not_1 (not_1_out, opCode[3]);
  and and_1 (branch, opCode[0], opCode[1], opCode[2], not_1_out);
endmodule

module controlUnit_ALUop (
  input  [3:0] opCode,
  output [2:0] ALUop
);

  wire and_1_out, and_2_out, and_3_out, and_4_out, and_5_out, not_1_out, not_2_out, not_3_out, not_4_out,
       not_5_out, not_6_out, not_7_out, not_8_out, not_9_out, not_10_out;

  not not_1 (not_1_out, opCode[2]);
  not not_2 (not_2_out, opCode[0]);
  not not_3 (not_3_out, opCode[3]);
  not not_4 (not_4_out, opCode[1]);
  not not_5 (not_5_out, opCode[0]);
  not not_6 (not_6_out, opCode[3]);
  not not_7 (not_7_out, opCode[2]);
  not not_8 (not_8_out, opCode[1]);
  not not_9 (not_9_out, opCode[2]);
  not not_10 (not_10_out, opCode[1]);
  and and_1 (and_1_out, not_1_out, opCode[1], opCode[0]);
  and and_2 (and_2_out, opCode[3], opCode[1], opCode[2], not_2_out);
  and and_3 (and_3_out, opCode[2], not_3_out, not_4_out, not_5_out);
  and and_4 (and_4_out, not_6_out, not_7_out, not_8_out);
  and and_5 (and_5_out, opCode[0], not_9_out, not_10_out);
  or or_1 (ALUop[0], and_1_out, and_2_out);
  or or_2 (ALUop[1], and_2_out, and_3_out);
  or or_3 (ALUop[2], and_4_out, and_5_out);

  // Other names for the same wires on the sheet: D = opCode[0]; C = opCode[1]; B = opCode[2]; A = opCode[3]
endmodule

module controlUnit_Memread (
  input  [3:0] opCode,
  output memRead
);

  wire and_1_out, and_2_out, not_1_out, not_2_out, not_3_out, not_4_out;

  not not_1 (not_1_out, opCode[1]);
  not not_2 (not_2_out, opCode[3]);
  not not_3 (not_3_out, opCode[3]);
  not not_4 (not_4_out, opCode[0]);
  and and_1 (and_1_out, not_2_out, opCode[2], not_1_out, opCode[0]);
  and and_2 (and_2_out, not_3_out, opCode[2], opCode[1], not_4_out);
  or or_1 (memRead, and_1_out, and_2_out);

  // Other names for the same wires on the sheet: D = opCode[0]; C = opCode[1]; B = opCode[2]; A = opCode[3]
endmodule

module controlUnit_ALUsrc (
  input  [3:0] opCode,
  output ALUsrc
);

  wire and_1_out, and_2_out, and_3_out, and_4_out, not_1_out, not_2_out, not_3_out, not_4_out, not_5_out,
       not_6_out;

  not not_1 (not_1_out, opCode[2]);
  not not_2 (not_2_out, opCode[2]);
  not not_3 (not_3_out, opCode[3]);
  not not_4 (not_4_out, opCode[1]);
  not not_5 (not_5_out, opCode[3]);
  not not_6 (not_6_out, opCode[0]);
  and and_1 (and_1_out, opCode[3], not_1_out, opCode[0]);
  and and_2 (and_2_out, opCode[3], not_2_out, opCode[1]);
  and and_3 (and_3_out, not_3_out, opCode[2], not_4_out, opCode[0]);
  and and_4 (and_4_out, not_5_out, opCode[2], opCode[1], not_6_out);
  or or_1 (ALUsrc, and_1_out, and_2_out, and_3_out, and_4_out);

  // Other names for the same wires on the sheet: D = opCode[0]; C = opCode[1]; B = opCode[2]; A = opCode[3]
endmodule

module controlUnit_RegDst (
  input  [3:0] opCode,
  output RegDst
);

  wire and_1_out, and_2_out, and_3_out, and_4_out, and_5_out, not_1_out, not_2_out, not_3_out, not_4_out,
       not_5_out, not_6_out;

  not not_1 (not_1_out, opCode[1]);
  not not_2 (not_2_out, opCode[2]);
  not not_3 (not_3_out, opCode[2]);
  not not_4 (not_4_out, opCode[1]);
  not not_5 (not_5_out, opCode[3]);
  not not_6 (not_6_out, opCode[0]);
  and and_1 (and_1_out, opCode[2], not_1_out, opCode[0]);
  and and_2 (and_2_out, opCode[3], not_2_out, opCode[0]);
  and and_3 (and_3_out, opCode[3], not_3_out, opCode[1]);
  and and_4 (and_4_out, opCode[3], opCode[2], not_4_out);
  and and_5 (and_5_out, not_5_out, opCode[2], opCode[1], not_6_out);
  or or_1 (RegDst, and_1_out, and_2_out, and_3_out, and_4_out, and_5_out);

  // Other names for the same wires on the sheet: D = opCode[0]; C = opCode[1]; B = opCode[2]; A = opCode[3]
endmodule

module controlUnit_RegWrite (
  input  [3:0] opCode,
  output RegWrite
);

  wire and_1_out, and_2_out, and_3_out, and_4_out, not_1_out, not_2_out, not_3_out, not_4_out, not_5_out;

  not not_1 (not_1_out, opCode[3]);
  not not_2 (not_2_out, opCode[2]);
  not not_3 (not_3_out, opCode[2]);
  not not_4 (not_4_out, opCode[1]);
  not not_5 (not_5_out, opCode[0]);
  and and_1 (and_1_out, not_1_out, not_2_out);
  and and_2 (and_2_out, opCode[0], not_3_out);
  and and_3 (and_3_out, opCode[2], not_4_out);
  and and_4 (and_4_out, opCode[3], opCode[1], not_5_out);
  or or_1 (RegWrite, and_1_out, and_2_out, and_3_out, and_4_out);

  // Other names for the same wires on the sheet: D = opCode[0]; C = opCode[1]; B = opCode[2]; A = opCode[3]
endmodule

// Control Unit
module controlUnit (
  input  [3:0] operation,
  output shift,
  output LorR,
  output carryin,
  output Bbar,
  output store,
  output load,
  output jump,
  output branch,
  output [2:0] ALUop,
  output memread,
  output ALUsrc,
  output regdst,
  output regwrite
);

  controlUnit_shift controlunit_shift_1 (.opCode(operation), .shift(shift));
  controlUnit_LorR controlunit_lorr_1 (.opCode(operation), .LorR(LorR));
  controlUnit_carryin controlunit_carryin_1 (.opCode(operation), .carryin(carryin));
  controlUnit_Bbar controlunit_bbar_1 (.opCode(operation), .Binvert(Bbar));
  controlUnit_store controlunit_store_1 (.opCode(operation), .store(store));
  controlUnit_load controlunit_load_1 (.opCode(operation), .load(load));
  controlUnit_jump controlunit_jump_1 (.opCode(operation), .jump(jump));
  controlUnit_branch controlunit_branch_1 (.opCode(operation), .branch(branch));
  controlUnit_ALUop controlunit_aluop_1 (.opCode(operation), .ALUop(ALUop));
  controlUnit_Memread controlunit_memread_1 (.opCode(operation), .memRead(memread));
  controlUnit_ALUsrc controlunit_alusrc_1 (.opCode(operation), .ALUsrc(ALUsrc));
  controlUnit_RegDst controlunit_regdst_1 (.opCode(operation), .RegDst(regdst));
  controlUnit_RegWrite controlunit_regwrite_1 (.opCode(operation), .RegWrite(regwrite));

  // Notes on the sheet:
  //   shift
  //   LorR
  //   carryin
  //   Bbar
  //   store
  //   load
  //   jump
  //   branch
  //   ALUop
  //   memread
  //   ALUsrc
  //   regdst
  //   regwrite
endmodule

module CPU (
  output OVF
);

  wire and_1_out, CLK_out, controlunit_1_alusrc, controlunit_1_bbar, controlunit_1_branch,
       controlunit_1_carryin, controlunit_1_jump, controlunit_1_lorr, controlunit_1_memread,
       controlunit_1_regdst, controlunit_1_regwrite, controlunit_1_shift, Lw, n16bit_alu_1_zero, sw;
  wire [2:0] controlunit_1_aluop;
  wire [3:0] multiplexer_1_out;
  wire [7:0] adder_1_out, adder_2_out, bit_extender_3_out, M, multiplexer_3_out, multiplexer_4_out, PC_q;
  wire [15:0] bit_extender_2_out, multiplexer_2_out, multiplexer_5_out, multiplexer_6_out,
       n16_bit_registerfile_1_read_data_1, n16_bit_registerfile_1_read_data_2, n16bit_alu_1_result,
       ram_1_data, rom_1_data, sll_srl_1_out_4;

  controlUnit controlunit_1 (
    .shift(controlunit_1_shift), .LorR(controlunit_1_lorr), .carryin(controlunit_1_carryin),
    .Bbar(controlunit_1_bbar), .store(sw), .load(Lw), .jump(controlunit_1_jump),
    .branch(controlunit_1_branch), .ALUop(controlunit_1_aluop), .memread(controlunit_1_memread),
    .ALUsrc(controlunit_1_alusrc), .regdst(controlunit_1_regdst), .regwrite(controlunit_1_regwrite),
    .operation(rom_1_data[15:12]));
  Register PC (.D(multiplexer_4_out), .Q(PC_q), .clk(CLK_out));  // open: en, clr
  Adder adder_1 (.a(PC_q), .b(8'h1), .out(adder_1_out));  // open: cin, cout
  Clock CLK (.out(CLK_out));
  ROM #(.dataWidth(16)) rom_1 (.addr(PC_q), .data(rom_1_data));  // open: sel
  Bit_Extender #(.in_width(12), .out_width(8)) bit_extender_1 (.in(rom_1_data[11:0]), .out(M));
  Multiplexer #(.width(4)) multiplexer_1 (
    .in0(rom_1_data[3:0]), .in1(rom_1_data[7:4]), .out(multiplexer_1_out), .sel(controlunit_1_regdst));  // open: en
  assign bit_extender_2_out = {{12{rom_1_data[3]}}, rom_1_data[3:0]};  // Bit_Extender bit_extender_2
  _16_bit_registerFile u_16_bit_registerfile_1 (
    .read_data_1(n16_bit_registerfile_1_read_data_1), .read_data_2(n16_bit_registerfile_1_read_data_2),
    .write_register(multiplexer_1_out), .write_data(multiplexer_6_out), .read_register_1(rom_1_data[11:8]),
    .read_register_2(rom_1_data[7:4]), .register_write(controlunit_1_regwrite), .clock(CLK_out));
  Bit_Extender #(.in_width(16), .out_width(8)) bit_extender_3 (.in(bit_extender_2_out), .out(bit_extender_3_out));
  Multiplexer #(.width(16)) multiplexer_2 (
    .in0(n16_bit_registerfile_1_read_data_2), .in1(bit_extender_2_out), .out(multiplexer_2_out),
    .sel(controlunit_1_alusrc));  // open: en
  Adder adder_2 (.a(adder_1_out), .b(bit_extender_3_out), .out(adder_2_out));  // open: cin, cout
  _16bit_ALU u_16bit_alu_1 (
    .A(n16_bit_registerfile_1_read_data_1), .B(multiplexer_2_out), .Binvert(controlunit_1_bbar),
    .operation(controlunit_1_aluop), .zero(n16bit_alu_1_zero), .overFlow(OVF),
    .carryin(controlunit_1_carryin), .result(n16bit_alu_1_result));  // open: carryOut
  sll_srl sll_srl_1 (
    .in_2(rom_1_data[3:0]), .in_3(controlunit_1_lorr), .out_4(sll_srl_1_out_4),
    .in_1(n16_bit_registerfile_1_read_data_1));
  and and_1 (and_1_out, controlunit_1_branch, n16bit_alu_1_zero);
  Multiplexer #(.width(8)) multiplexer_3 (
    .in0(adder_1_out), .in1(adder_2_out), .out(multiplexer_3_out), .sel(and_1_out));  // open: en
  Multiplexer #(.width(8)) multiplexer_4 (
    .in0(multiplexer_3_out), .in1(M), .out(multiplexer_4_out), .sel(controlunit_1_jump));  // open: en
  Multiplexer #(.width(16)) multiplexer_5 (
    .in0(n16bit_alu_1_result), .in1(ram_1_data), .out(multiplexer_5_out), .sel(controlunit_1_memread));  // open: en
  RAM #(.addrWidth(16), .dataWidth(16), .bus("separate")) ram_1 (
    .addr(n16bit_alu_1_result), .din(n16_bit_registerfile_1_read_data_2), .data(ram_1_data), .str(sw),
    .clk(CLK_out), .ld(Lw));  // open: sel, clr
  Multiplexer #(.width(16)) multiplexer_6 (
    .in0(multiplexer_5_out), .in1(sll_srl_1_out_4), .out(multiplexer_6_out), .sel(controlunit_1_shift));  // open: en

  // Notes on the sheet:
  //   0000 0010 0011 0101
  //   LorR
  //   C\in
  //   shift
  //   opCode
  //   store
  //   B'
  //   Instruction Memory
  //   branch
  //   jump
  //   load
  //   contents of rom_1 (hex, n*v repeats v):
  //   9011 9021 9035 9051 735b 9551 204 122 401 f004 6520 117*0 d792 6a92
  //   Memread
  //   ALUop
  //   ALUsrc
  //   RegDst
  //   RegWrite
  //   overFlow
  //   carryOut
  //   Data Memory
endmodule
