// Logisim project registerFile.circ as structural Verilog: 1 circuit, main circuit main
module main (
  input  [3:0] read_register_1,
  input  [3:0] write_register,
  input  [3:0] read_register_2,
  input  [15:0] write_data,
  input  register_write,
  input  clock,
  output [15:0] read_data_1,
  output [15:0] read_data_2
);

  wire and_1_out, and_2_out, and_3_out, and_4_out, and_5_out, and_6_out, and_7_out, and_8_out, and_9_out,
       and_10_out, and_11_out, and_12_out, and_13_out, and_14_out, and_15_out, and_16_out, decoder_1_out0,
       decoder_1_out1, decoder_1_out2, decoder_1_out3, decoder_1_out4, decoder_1_out5, decoder_1_out6,
       decoder_1_out7, decoder_1_out8, decoder_1_out9, decoder_1_out10, decoder_1_out11, decoder_1_out12,
       decoder_1_out13, decoder_1_out14, decoder_1_out15;
  wire [15:0] a0_q, a1_q, ra_q, s0_q, s1_q, s2_q, s3_q, s4_q, s5_q, sp_q, t0_q, t1_q, t2_q, t3_q, v0_q,
       zero_q;

  Decoder #(.select(4)) decoder_1 (
    .out0(decoder_1_out0), .out1(decoder_1_out1), .out2(decoder_1_out2), .out3(decoder_1_out3),
    .out4(decoder_1_out4), .out5(decoder_1_out5), .out6(decoder_1_out6), .out7(decoder_1_out7),
    .out8(decoder_1_out8), .out9(decoder_1_out9), .out10(decoder_1_out10), .out11(decoder_1_out11),
    .out12(decoder_1_out12), .out13(decoder_1_out13), .out14(decoder_1_out14), .out15(decoder_1_out15),
    .sel(write_register));  // open: en
  and and_1 (and_1_out, decoder_1_out0, register_write);
  and and_2 (and_2_out, decoder_1_out1, register_write);
  and and_3 (and_3_out, decoder_1_out2, register_write);
  and and_4 (and_4_out, decoder_1_out3, register_write);
  and and_5 (and_5_out, decoder_1_out4, register_write);
  and and_6 (and_6_out, decoder_1_out5, register_write);
  and and_7 (and_7_out, decoder_1_out6, register_write);
  and and_8 (and_8_out, decoder_1_out7, register_write);
  and and_9 (and_9_out, decoder_1_out8, register_write);
  and and_10 (and_10_out, decoder_1_out9, register_write);
  and and_11 (and_11_out, decoder_1_out10, register_write);
  and and_12 (and_12_out, decoder_1_out11, register_write);
  and and_13 (and_13_out, decoder_1_out12, register_write);
  and and_14 (and_14_out, decoder_1_out13, register_write);
  and and_15 (and_15_out, decoder_1_out14, register_write);
  and and_16 (and_16_out, decoder_1_out15, register_write);
  Register #(.width(16)) zero (.D(write_data), .en(and_1_out), .Q(zero_q), .clr(clock));  // open: clk
  Register #(.width(16)) t0 (.D(write_data), .en(and_2_out), .Q(t0_q), .clr(clock));  // open: clk
  Register #(.width(16)) t1 (.D(write_data), .en(and_3_out), .Q(t1_q), .clr(clock));  // open: clk
  Register #(.width(16)) t2 (.D(write_data), .en(and_4_out), .Q(t2_q), .clr(clock));  // open: clk
  Register #(.width(16)) t3 (.D(write_data), .en(and_5_out), .Q(t3_q), .clr(clock));  // open: clk
  Register #(.width(16)) s0 (.D(write_data), .en(and_6_out), .Q(s0_q), .clr(clock));  // open: clk
  Register #(.width(16)) s1 (.D(write_data), .en(and_7_out), .Q(s1_q), .clr(clock));  // open: clk
  Register #(.width(16)) s2 (.D(write_data), .en(and_8_out), .Q(s2_q), .clr(clock));  // open: clk
  Register #(.width(16)) s3 (.D(write_data), .en(and_9_out), .Q(s3_q), .clr(clock));  // open: clk
  Register #(.width(16)) s4 (.D(write_data), .en(and_10_out), .Q(s4_q), .clr(clock));  // open: clk
  Register #(.width(16)) s5 (.D(write_data), .en(and_11_out), .Q(s5_q), .clr(clock));  // open: clk
  Register #(.width(16)) sp (.D(write_data), .en(and_12_out), .Q(sp_q), .clr(clock));  // open: clk
  Register #(.width(16)) v0 (.D(write_data), .en(and_13_out), .Q(v0_q), .clr(clock));  // open: clk
  Register #(.width(16)) ra (.D(write_data), .en(and_14_out), .Q(ra_q), .clr(clock));  // open: clk
  Register #(.width(16)) a0 (.D(write_data), .en(and_15_out), .Q(a0_q), .clr(clock));  // open: clk
  Register #(.width(16)) a1 (.D(write_data), .en(and_16_out), .Q(a1_q), .clr(clock));  // open: clk
  Multiplexer #(.select(4), .width(16)) multiplexer_1 (
    .in0(zero_q), .in1(t0_q), .in2(t1_q), .in3(t2_q), .in4(t3_q), .in5(s0_q), .in6(s1_q), .in7(s2_q),
    .in8(s3_q), .in9(s4_q), .in10(s5_q), .in11(sp_q), .in12(v0_q), .in13(ra_q), .in14(a0_q), .in15(a1_q),
    .out(read_data_1), .sel(read_register_1));  // open: en
  Multiplexer #(.select(4), .width(16)) multiplexer_2 (
    .in0(zero_q), .in1(t0_q), .in2(t1_q), .in3(t2_q), .in4(t3_q), .in5(s0_q), .in6(s1_q), .in7(s2_q),
    .in8(s3_q), .in9(s4_q), .in10(s5_q), .in11(sp_q), .in12(v0_q), .in13(ra_q), .in14(a0_q), .in15(a1_q),
    .out(read_data_2), .sel(read_register_2));  // open: en
endmodule
